# Fritzing sketch Untitled Sketch (saved by Fritzing 0.9.3b)
circuit board: 6.8908cm x 5.45804cm
breadboards: 1

parts:
  S1 = Pushbutton [package="[THT]"]
  S2 = Pushbutton [package="[THT]"]
  LED1 = LED - 5mm [color="Red (633nm)" package="5 mm [THT]"]
  R1 = Resistor [tolerance=±5% resistance=220 package=THT]
  Componente1 = Arduino Uno (Rev3)
  R2 = Resistor [tolerance=±5% resistance=10k package=THT]
  R3 = Resistor [tolerance=±5% resistance=10k package=THT]

nets:
  N1: S1.Pin_1, S1.Pin_2, Componente1.D7, R3.Pin_0
  N2: S1.Pin_3, S1.Pin_4, S2.Pin_3, S2.Pin_4, Componente1.5V
  N3: S2.Pin_1, S2.Pin_2, Componente1.D2, R2.Pin_0
  N4: LED1.cathode, R1.Pin_0
  N5: LED1.anode, Componente1.D13/SCK
  N6: R1.Pin_1, Componente1.GND, R2.Pin_1, R3.Pin_1
